# Fritzing sketch input_output (saved by Fritzing 0.9.4)
breadboards: 1

parts:
  Bauteil1 = Tessel 2
  U1 = Optocoupler [package=THT]
  R1 = Resistor [tolerance=±5% resistance=330 package=THT]
  R2 = Resistor [tolerance=±5% resistance=330 package=THT]
  R4 = Resistor [tolerance=±5% resistance=10k package=THT]
  R5 = Resistor [tolerance=±5% resistance=10k package=THT]
  U2 = Optocoupler [package=THT]
  IC1 = IC, DIP package, 16 pins [chip_label=CS2105GP-M12]
  U3 = Optocoupler [package=THT]
  R6 = Resistor [tolerance=±5% resistance=10k package=THT]
  R7 = Resistor [tolerance=±5% resistance=68 package=THT]

nets:
  N1: Bauteil1.GND, R4.Pin_1, R5.Pin_1, U3.Pin_2
  N2: Bauteil1.3V3, U1.Pin_5, U2.Pin_5
  N3: Bauteil1.2, U1.Pin_4, R4.Pin_0
  N4: Bauteil1.5, R5.Pin_0, U2.Pin_4
  N5: Bauteil1.7, R7.Pin_1
  N6: U1.Pin_1, R1.Pin_1
  N7: U1.Pin_2, U2.Pin_2, IC1.pin14, U3.Pin_4
  N8: R1.Pin_0, IC1.pin7
  N9: R2.Pin_0, IC1.pin11
  N10: R2.Pin_1, U2.Pin_1
  N11: IC1.pin5, R6.Pin_1
  N12: IC1.pin16, U3.Pin_5, R6.Pin_0
  N13: U3.Pin_1, R7.Pin_0

custom parts:
  Tessel 2: Draft version of Tessel 2
